# Fritzing sketch 96 well RGB panel wiring example (saved by Fritzing 0.9.3b)

parts:
  Part1 = Arduino Uno (Rev3) - ICSP
  IC1 = DIP - 6 pins [chip_label=IC package="DIP (Dual Inline) [THT]"]
  S1 = 96 well RGB light guide [package=THT]

nets:
  N1: Part1.D6_PWM, IC1.data-in
  N2: Part1.GND, IC1.gnd-in
  N3: Part1.VIN, IC1.5v-in
  N4: IC1.5v-out, S1.5V
  N5: IC1.data-out, S1.DATA
  N6: IC1.gnd-out, S1.GND

custom parts:
  DIP - 6 pins: A DIP stand-in part for whatever IC you want. With 6 pins on a 300mil dual inline package (DIP) footprint.
